# Fritzing sketch wiring-diagram (saved by Fritzing 1.0.4)

parts:
  Part1 = Adafruit ESP32-S3 Reverse TFT Feather [part_number="Adafruit #5691"]
  Q1 = PNP-Transistor [package="SOT-23 [SMD]"]
  F1 = Fan - Ventilador [package=THT]
  R1 = Resistor [tolerance=±5% resistance=1k package="1206 [SMD]"]  # not connected
  Part2 = Adafruit SCD4x [part_number="Adafruit #5187"]

nets:
  GND: Part1.GND, Q1.2, Part2.GND
  N1: Part1.VSENSOR, Part2.VCC
  N2: Part1.SDA, Part2.SDA
  N3: Part1.SCL, Part2.SCL
  N4: Part1.VBUS, F1.5V
  N5: Q1.1, F1.GND

custom parts:
  Fan - Ventilador: Ventilador de 2 pines, se encuentra comunmente en computadoras de escritorio
  Adafruit SCD4x: Take a deep breath in...now slowly breathe out. Mmm isn't it wonderful? All that air around us, which we bring into our lungs, extracts oxygen from and then breathes out carbon dioxide. CO2 is essential for life on this planet we call Earth - we and plants take turns using and emitting CO2 in an elegant symbiosis. But it's important to keep that CO2 balanced - you don't want too much around,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
